# Fritzing sketch circuit_promini_oled_joystick_2matrices (saved by Fritzing 0.9.3b)

parts:
  Part1 = Thumb Joystick
  Part2 = Arduino Pro Mini v13
  Part3 = NeoPixel NeoMatrix 8x8 [part_number=1487]
  Part5 = NeoPixel NeoMatrix 8x8 [part_number=1487]
  Grove1 = Grove OLED 128x96
  U1 = LIPO-1000mAh [package=lipo-1000]
  C3 = Capacitor Polarized [package=cpol-radial-100uf-25v]
  C4 = Capacitor Polarized [package=cpol-radial-100uf-25v]

nets:
  GND: Part1.GND, Part2.GND, Part3.GND, Part5.GND, Grove1.GND, U1.-, C3.-, C4.-
  N1: Part1.HORZ, Part2.A0
  N2: Part1.VERT, Part2.A1
  VCC: Part1.VCC, Part2.VCC, Part3.VDD, Part5.VDD, Grove1.VCC, U1.+, C3.+, C4.+
  N3: Part2.A4, Grove1.SDA
  N4: Part2.A5, Grove1.SCL
  N5: Part2.D6_PWM, Part5.IN
  N6: Part2.D5_PWM, Part3.IN

custom parts:
  NeoPixel NeoMatrix 8x8: Put on your sunglasses before wiring up this LED matrix - 64 eye-blistering RGB LEDs adorn the NeoMatrix for a blast of configurable color. Arranged in an 8x8 matrix, each pixel is individually addressable. Only one microcontroller pin is required to control all the LEDs, and you get 24 bit color for each LED.
