# Fritzing sketch circuit (saved by Fritzing 0.9.3b)

parts:
  Part1 = Arduino Uno (Rev3)
  Part2 = 16 NeoPixel Ring [part_number=1463]  # not connected
  Part3 = NeoPixel NeoMatrix 8x8 [part_number=1487]
  Part4 = NeoPixel NeoMatrix 8x8 [part_number=1487]
  U2 = Thumb Joystick [package=joystick]

nets:
  N1: Part1.A4/SDA, U2.H+
  N2: Part1.A5/SCL, U2.SEL+
  N3: Part1.D3_PWM, Part4.IN
  N4: Part1.D6_PWM, Part3.IN

custom parts:
  16 NeoPixel Ring: 16 ultra bright smart LED NeoPixels are arranged in a circle with 1.75" (44.5mm) outer diameter. The rings are 'chainable' - connect the output pin of one to the input pin of another. Use only one microcontroller pin to control as many as you can chain together! Each LED is addressable as the driver chip is inside the LED. Each one has ~18mA constant current drive so the color will be very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
  NeoPixel NeoMatrix 8x8: Put on your sunglasses before wiring up this LED matrix - 64 eye-blistering RGB LEDs adorn the NeoMatrix for a blast of configurable color. Arranged in an 8x8 matrix, each pixel is individually addressable. Only one microcontroller pin is required to control all the LEDs, and you get 24 bit color for each LED.
